# Fritzing sketch BBB (saved by Fritzing 0.9.3b)
breadboards: 1

parts:
  LCD1 = LCD screen
  R2 = Resistor [tolerance=±5% resistance=220 package=THT]
  R1 = Rotary Potentiometer (Small) [maximum_resistance=10kΩ package=THT]
  BeagleBone1 = BeagleBone Black

nets:
  N1: LCD1.VSS, LCD1.R/W, LCD1.LED-, R1.leg2, BeagleBone1.no_name_yet#105
  N2: LCD1.VDD, R2.Pin_1, R1.leg1, BeagleBone1.no_name_yet#104
  N3: LCD1.V0, R1.wiper
  N4: LCD1.RS, BeagleBone1.no_name_yet#122
  N5: LCD1.E, BeagleBone1.no_name_yet#118
  N6: LCD1.DB4, BeagleBone1.no_name_yet#111
  N7: LCD1.DB5, BeagleBone1.no_name_yet#115
  N8: LCD1.DB6, BeagleBone1.no_name_yet#116
  N9: LCD1.DB7, BeagleBone1.no_name_yet#112
  N10: LCD1.LED+, R2.Pin_0

custom parts:
  BeagleBone Black: BeagleBone Black rev. A5B
