# Fritzing sketch Pi3 (saved by Fritzing 0.9.3b)
breadboards: 1

parts:
  LCD1 = LCD screen
  R2 = Resistor [tolerance=±5% resistance=220 package=THT]
  R1 = Rotary Potentiometer (Small) [maximum_resistance=10kΩ package=THT]
  Raspberry_Pi_Zero1 = Raspberry Pi 3 [part_number=RPI-3-V1.2]

nets:
  VSS: LCD1.VSS, LCD1.R/W, LCD1.LED-, R1.leg2, Raspberry_Pi_Zero1.GND
  VDD: LCD1.VDD, R2.Pin_1, R1.leg1, Raspberry_Pi_Zero1.5V
  N1: LCD1.V0, R1.wiper
  N2: LCD1.RS, Raspberry_Pi_Zero1.GIPO25
  N3: LCD1.E, Raspberry_Pi_Zero1.GIPO24
  N4: LCD1.DB4, Raspberry_Pi_Zero1.GIPO17
  N5: LCD1.DB5, Raspberry_Pi_Zero1.GIPO22
  N6: LCD1.DB6, Raspberry_Pi_Zero1.GIPO23
  N7: LCD1.DB7, Raspberry_Pi_Zero1.GIPO18
  N8: LCD1.LED+, R2.Pin_0
