# Fritzing sketch PiZero (saved by Fritzing 0.9.3b)
breadboards: 1

parts:
  Raspberry_Pi_Zero1 = Raspberry Pi Zero
  LCD1 = LCD screen
  R2 = Resistor [tolerance=±5% resistance=220 package=THT]
  R1 = Rotary Potentiometer (Small) [maximum_resistance=10kΩ package=THT]

nets:
  N1: Raspberry_Pi_Zero1.GPIO17, LCD1.DB4
  N2: Raspberry_Pi_Zero1.GPIO22, LCD1.DB5
  N3: Raspberry_Pi_Zero1.GPIO25, LCD1.RS
  N4: Raspberry_Pi_Zero1.GPIO24, LCD1.E
  N5: Raspberry_Pi_Zero1.GPIO23, LCD1.DB6
  N6: Raspberry_Pi_Zero1.GPIO18, LCD1.DB7
  GND: Raspberry_Pi_Zero1.GND, LCD1.VSS, LCD1.R/W, LCD1.LED-, R1.leg2
  5V: Raspberry_Pi_Zero1.5V, LCD1.VDD, R2.Pin_1, R1.leg1
  N7: LCD1.V0, R1.wiper
  N8: LCD1.LED+, R2.Pin_0
